# Fritzing sketch Blink (saved by Fritzing 0.8.3b)
circuit board: 6.88561cm x 5.36311cm
circuit board: 6.88561cm x 5.36311cm
breadboards: 1

parts:
  Arduino1 = Arduino Uno (Rev3)
  Arduino2 = Arduino Uno (Rev3)
  LED1 = LED - 5mm [color="Red (633nm)" package="5 mm [THT]"]
  LED3 = smd LED [color="Red (633nm)" package="1206 [SMD]"]  # not connected
  R1 = Resistor [tolerance=±5% resistance=220 package=THT]
  LED4 = LED - 5mm [color="Red (633nm)" package="5 mm [THT]"]

nets:
  N1: Arduino1.GND, R1.Pin_1
  N2: Arduino1.D13/SCK, LED4.anode
  N3: Arduino2.D13/SCK, LED1.anode
  N4: Arduino2.GND, LED1.cathode
  N5: R1.Pin_0, LED4.cathode

notes:
  While the version above will work, it might damage the LED after some time. Better limit the current that runs through it by adding a resistor.
  The right resistor value can be
  calculated like this.
  In this very simple example, Arduino will be programmed to blink the LED on pin 13.
  Related Arduino example:
  http://arduino.cc/en/Tutorial/Blink

// code stored in the sketch: Blink.ino
/*
  Blink
  Turns on an LED on for one second, then off for one second, repeatedly.
 
  This example code is in the public domain.
 */

void setup() {                
  // initialize the digital pin as an output.
  // Pin 13 has an LED connected on most Arduino boards:
  pinMode(13, OUTPUT);     
}

void loop() {
  digitalWrite(13, HIGH);   // set the LED on
  delay(1000);              // wait for a second
  digitalWrite(13, LOW);    // set the LED off
  delay(1000);              // wait for a second
}
